# Fritzing sketch 1 (saved by Fritzing 1.0.1rc)

parts:
  WeMos_D1_Mini1 = WeMos D1 Mini
  KY-1 = Keyes Relay [package=THT]
  HC-SR04_Sensor_1 = HC-SR04 Ultrasonic Distance Sensor

nets:
  N1: WeMos_D1_Mini1.3V3, KY-1.power
  5V: WeMos_D1_Mini1.5V, HC-SR04_Sensor_1.VCC
  N2: WeMos_D1_Mini1.D2, HC-SR04_Sensor_1.ECHO
  N3: WeMos_D1_Mini1.D3, HC-SR04_Sensor_1.TRIG
  N4: WeMos_D1_Mini1.D7, KY-1.signal
  N5: WeMos_D1_Mini1.G, KY-1.ground, HC-SR04_Sensor_1.GND

custom parts:
  Keyes Relay: The Keyes 5V relay module is suitable for SCM development, home appliance control. It uses a 5V~12V TIL control signal which can control DC / AC signal.
