# Fritzing sketch dev1 (saved by Fritzing 1.0.1rc)

parts:
  WeMos_D1_Mini1 = WeMos D1 Mini
  HC-SR04_Sensor_1 = HC-SR04 Ultrasonic Distance Sensor
  HC-SR04_Sensor_2 = HC-SR04 Ultrasonic Distance Sensor
  KY-1 = Keyes Relay [package=THT]
  KY-2 = Keyes Relay [package=THT]
  S1 = Momentary Switch [package=ksa_sealed_tac_switch]
  S2 = SPST Switch [package=switch-spdt-smd]
  S3 = SPST Switch [package=switch-spdt-smd]
  LED1 = smd LED [color="Red (633nm)" package="1206 [SMD]"]
  LED2 = LED - 5mm [color="Blue (525nm)" current=0.030 package="5 mm [THT]"]
  LED3 = LED - 5mm [color="Blue (525nm)" current=0.030 package="5 mm [THT]"]

nets:
  N1: WeMos_D1_Mini1.3V3, S2.P, S3.P
  VCC: WeMos_D1_Mini1.5V, HC-SR04_Sensor_1.VCC, HC-SR04_Sensor_2.VCC, KY-1.power, KY-2.power
  N2: WeMos_D1_Mini1.D1, KY-2.signal, S3.O, LED3.anode
  N3: WeMos_D1_Mini1.D2, KY-1.signal, S2.O, LED2.anode
  N4: WeMos_D1_Mini1.D3, LED1.anode
  N5: WeMos_D1_Mini1.D5, HC-SR04_Sensor_2.TRIG
  N6: WeMos_D1_Mini1.D6, HC-SR04_Sensor_2.ECHO
  N7: WeMos_D1_Mini1.D7, HC-SR04_Sensor_1.ECHO
  N8: WeMos_D1_Mini1.D8, HC-SR04_Sensor_1.TRIG
  GND: WeMos_D1_Mini1.G, HC-SR04_Sensor_1.GND, HC-SR04_Sensor_2.GND, KY-1.ground, KY-2.ground, S1.1, LED1.cathode, LED2.cathode, LED3.cathode
  N9: WeMos_D1_Mini1.RST, S1.3

custom parts:
  Keyes Relay: The Keyes 5V relay module is suitable for SCM development, home appliance control. It uses a 5V~12V TIL control signal which can control DC / AC signal.
