# Fritzing sketch dev2 (saved by Fritzing 1.0.1rc)

parts:
  KY-1 = Keyes Relay [package=THT]
  YF-S201_Flow_Meter1 = YF-S201 Water Flow Meter
  VALVE1 = Plastic Solenoid Valve
  Power_plug1 = Power plug
  WeMos_D1_Mini1 = WeMos D1 Mini
  LED1 = smd LED [color="Red (633nm)" package="1206 [SMD]"]
  S1 = Momentary Switch [package=ksa_sealed_tac_switch]
  LED2 = LED - 5mm [color="Blue (525nm)" current=0.030 package="5 mm [THT]"]

nets:
  N1: KY-1.signal, WeMos_D1_Mini1.D2, LED2.anode
  VCC: KY-1.power, YF-S201_Flow_Meter1.VCC, WeMos_D1_Mini1.5V
  N2: KY-1.ground, YF-S201_Flow_Meter1.GND, WeMos_D1_Mini1.G, LED1.cathode, S1.4, LED2.cathode
  N3: KY-1.NC, VALVE1.no_name_yet#1
  N4: KY-1.C, Power_plug1.VCC
  N5: YF-S201_Flow_Meter1.SIG, WeMos_D1_Mini1.D1
  N6: VALVE1.no_name_yet#2, Power_plug1.GND
  N7: WeMos_D1_Mini1.D3, LED1.anode
  N8: WeMos_D1_Mini1.RST, S1.2

custom parts:
  Keyes Relay: The Keyes 5V relay module is suitable for SCM development, home appliance control. It uses a 5V~12V TIL control signal which can control DC / AC signal.
  YF-S201 Water Flow Meter: The YF-S201 Flow Meter. The input voltage is 5V to 24V (DC).
