# Fritzing sketch water flow (saved by Fritzing 1.0.1rc)

parts:
  YF-S201_Flow_Meter1 = YF-S201 Water Flow Meter
  WeMos_D1_Mini1 = WeMos D1 Mini

nets:
  N1: YF-S201_Flow_Meter1.SIG, WeMos_D1_Mini1.A0
  N2: YF-S201_Flow_Meter1.GND, WeMos_D1_Mini1.G
  VCC: YF-S201_Flow_Meter1.VCC, WeMos_D1_Mini1.5V

custom parts:
  YF-S201 Water Flow Meter: The YF-S201 Flow Meter. The input voltage is 5V to 24V (DC).
