# Fritzing sketch Sketch (saved by Fritzing 0.9.6b)

parts:
  YF-S201_Flow_Meter1 = YF-S201 Water Flow Meter
  WeMos_D1_Mini1 = WeMos D1 Mini
  SEN1 = US-100 Ultrasonic Distance Sensor
  KY-1 = Keyes Relay [package=THT]

nets:
  N1: YF-S201_Flow_Meter1.SIG, WeMos_D1_Mini1.A0
  GND: YF-S201_Flow_Meter1.GND, WeMos_D1_Mini1.G, SEN1.GND, KY-1.ground
  VCC: YF-S201_Flow_Meter1.VCC, WeMos_D1_Mini1.5V, SEN1.VCC
  N2: WeMos_D1_Mini1.3V3, KY-1.power
  N3: WeMos_D1_Mini1.D2, SEN1.TRIG
  N4: WeMos_D1_Mini1.D3, SEN1.ECHO
  N5: WeMos_D1_Mini1.D5, KY-1.signal

custom parts:
  YF-S201 Water Flow Meter: The YF-S201 Flow Meter. The input voltage is 5V to 24V (DC).
  Keyes Relay: The Keyes 5V relay module is suitable for SCM development, home appliance control. It uses a 5V~12V TIL control signal which can control DC / AC signal.
